# Fritzing sketch MontageLecteurRFID (saved by Fritzing 0.9.3b)
breadboards: 1

parts:
  Composant1 = RFID-RC522-v3
  Raspberry_Pi_1 = Raspberry Pi 3 [part_number=RPI-3-V1.2]
  LED1 = LED - 3mm [color="Red (633nm)" package="3 mm [THT]"]
  LED2 = LED - 3mm [color="Green (555nm)" package="3 mm [THT]"]
  R1 = Resistor [tolerance=±5% resistance=220 package=THT]

nets:
  N1: Composant1.SDA, Raspberry_Pi_1.GIPO8
  N2: Composant1.SCK, Raspberry_Pi_1.GIPO11
  N3: Composant1.MOSI, Raspberry_Pi_1.GIPO10
  N4: Composant1.MISO, Raspberry_Pi_1.GIPO9
  N5: Composant1.IRQ, Raspberry_Pi_1.GIPO24
  GND: Composant1.GND, Raspberry_Pi_1.GND, R1.Pin_0
  N6: Composant1.RST, Raspberry_Pi_1.GIPO25
  3.3V: Composant1.3.3V, Raspberry_Pi_1.3V3
  N7: Raspberry_Pi_1.GPIO2, LED1.anode
  N8: Raspberry_Pi_1.GPIO3, LED1.cathode, LED2.cathode, R1.Pin_1

custom parts:
  RFID-RC522-v3: A simple China made RFID-RC522 Reader (6x4 cm); do check the pin labels, as this is a MFRC522 based clone.

// code stored in the sketch: LectureRFIDino.ino
import RPi.GPIO as GPIO
import MFRC522

# Création d'un objet MFRC522
MIFAREReader = MFRC522.MFRC522()

# Boucle infinie pour lire les cartes
while True:
    # Recherche de cartes RFID
    (status, TagType) = MIFAREReader.MFRC522_Request(MIFAREReader.PICC_REQIDL)

    # Si une carte est détectée
    if status == MIFAREReader.MI_OK:
        print("Carte détectée")
    
    # Récupération de l'UID de la carte
    (status, uid) = MIFAREReader.MFRC522_Anticoll()
    
    # Si l'UID est lu avec succès
    if status == MIFAREReader.MI_OK:
        # Affiche l'UID de la carte
        print("UID de la carte : " + str(uid[0]) + "," + str(uid[1]) + "," + str(uid[2]) + "," + str(uid[3]))
